// Digital circuit small.dig as structural Verilog
module \small  (
  input  A,
  input  B,
  output Y
);

  wire not_1_out, or_1_out;

  or or_1 (or_1_out, A, B);
  not not_1 (not_1_out, B);
  and and_1 (Y, or_1_out, not_1_out);
endmodule
