// Digital circuit alu_1bit_2gatemux.dig as structural Verilog
module alu_1bit_2gatemux (
  input  A,
  input  B,
  input  Cin,
  input  Op_0,
  input  B_inv,
  input  Op_1,
  output Cout,
  output Y
);

  wire and_1_out, and_2_out, and_3_out, and_4_out, and_5_out, and_6_out, and_7_out, and_8_out, and_9_out,
       and_10_out, not_1_out, not_2_out, or_1_out, or_3_out, or_4_out, xor_1_out, xor_2_out, xor_3_out;

  xor xor_1 (xor_1_out, B, B_inv);
  or or_1 (or_1_out, A, xor_1_out);
  and and_1 (and_1_out, A, xor_1_out);
  xor xor_2 (xor_2_out, A, xor_1_out);
  xor xor_3 (xor_3_out, xor_2_out, Cin);
  and and_2 (and_2_out, xor_2_out, Cin);
  or or_2 (Cout, and_2_out, and_1_out);
  not not_1 (not_1_out, Op_0);
  not not_2 (not_2_out, Op_1);
  and and_3 (and_3_out, not_1_out, not_2_out);
  and and_4 (and_4_out, Op_0, not_2_out);
  and and_5 (and_5_out, not_1_out, Op_1);
  and and_6 (and_6_out, Op_0, Op_1);
  and and_7 (and_7_out, or_1_out, and_3_out);
  and and_8 (and_8_out, and_1_out, and_4_out);
  and and_9 (and_9_out, xor_2_out, and_5_out);
  and and_10 (and_10_out, xor_3_out, and_6_out);
  or or_3 (or_3_out, and_7_out, and_8_out);
  or or_4 (or_4_out, and_9_out, and_10_out);
  or or_5 (Y, or_3_out, or_4_out);
endmodule
